# Fritzing sketch Tube Controller v1 (saved by Fritzing 0.7.11b)
stripboards: 1

parts:
  Arduino = Arduino Pro Mini 3.3V
  Mic = Breakout Board for Electret Microphone
  FET_R = Basic FET P-Channel [package="TO220 [THT]"]
  FET_G = Basic FET P-Channel [package="TO220 [THT]"]
  FET_B = Basic FET P-Channel [package="TO220 [THT]"]
  BUTTONS = male pin header, 7 pins [form="♂ (male)"]
  RGB_LED = male pin header, 5 pins [form="♂ (male)"]
  R4 = Resistor [tolerance=±5% resistance=220 package=THT]
  240v = screw terminal, 4 pins
  SSR = Pushbutton [package=THT]
  POWER = 2.1mm DC Barrel Jack
  BUZZ = Piezo Speaker
  SSR_2 = LED - 5mm [color="Red (633nm)" package="5 mm [THT]"]
  R1 = Resistor [tolerance=±5% resistance=220 package=THT]
  R2 = Resistor [tolerance=±5% resistance=220 package=THT]
  R3 = Resistor [tolerance=±5% resistance=220 package=THT]

nets (from the schematic view):
  N1: Arduino.RAW, RGB_LED.pin1, POWER.center
  GND: Arduino.GND, Mic.GND, FET_R.source, FET_G.source, FET_B.source, POWER.sleeve, BUZZ.pin1, SSR_2.cathode, R1.Pin_1, R2.Pin_1, R3.Pin_1
  VCC: Arduino.VCC, Mic.VCC
  N2: Arduino.A2, Mic.AUD
  N3: Arduino.SCK, BUZZ.pin2
  N4: Arduino.MISO, R4.Pin_0
  N5: Arduino.MOSI, FET_R.gate, R3.Pin_0
  N6: Arduino.D10, FET_G.gate, R2.Pin_0
  N7: Arduino.D9, FET_B.gate, R1.Pin_0
  N8: Arduino.D8, BUTTONS.pin1
  N9: Arduino.D7, BUTTONS.pin2
  N10: Arduino.D6, BUTTONS.pin3
  N11: Arduino.D5, BUTTONS.pin4
  N12: Arduino.D4, BUTTONS.pin5
  N13: Arduino.D3, BUTTONS.pin6
  N14: Arduino.D2, BUTTONS.pin7
  N15: FET_R.drain, RGB_LED.pin3
  N16: FET_G.drain, RGB_LED.pin4
  N17: FET_B.drain, RGB_LED.pin5
  N18: R4.Pin_1, SSR_2.anode
  N19: 240v.pin1, SSR.leg0
  N20: 240v.pin2, 240v.pin3
  N21: 240v.pin4, SSR.leg1

custom parts:
  2.1mm DC Barrel Jack: 2.1mm DC Barrel Jack with Thru-Hole Connectors (breadboardable)
